// Logisim project CRC_Check_713_13.circ as structural Verilog
module CRC (
  input  [7:0] A,
  input  [3:0] B,
  output [10:0] C
);

  _8b_checker u_8b_checker_1 (.A(A), .B(B), .Mod(C[2:0]));

  assign C[10:3] = A;
endmodule

module _4b_mod2_divider (
  input  [3:0] A,
  input  [3:0] B,
  output D,
  output [2:0] C
);

  wire [2:0] xor_1_out;

  assign xor_1_out = A[2:0] ^ B[2:0];  // XOR_Gate xor_1, 3 bits wide
  Multiplexer #(.width(3), .enable("false")) multiplexer_1 (.in0(A[2:0]), .in1(xor_1_out), .out(C), .sel(A[3]));

  assign D = A[3];
endmodule

module _8b_checker (
  input  [7:0] A,
  input  [3:0] B,
  output [2:0] Mod
);

  wire [2:0] n4b_mod2_divider_1_c, n4b_mod2_divider_2_c, n4b_mod2_divider_3_c, n4b_mod2_divider_4_c,
       n4b_mod2_divider_5_c, n4b_mod2_divider_6_c, n4b_mod2_divider_7_c;

  _4b_mod2_divider u_4b_mod2_divider_1 (.A(A[7:4]), .B(B), .C(n4b_mod2_divider_1_c));  // open: D
  _4b_mod2_divider u_4b_mod2_divider_2 (.A({n4b_mod2_divider_1_c, A[3]}), .B(B), .C(n4b_mod2_divider_2_c));  // open: D
  _4b_mod2_divider u_4b_mod2_divider_3 (.A({n4b_mod2_divider_2_c, A[2]}), .B(B), .C(n4b_mod2_divider_3_c));  // open: D
  _4b_mod2_divider u_4b_mod2_divider_4 (.A({n4b_mod2_divider_3_c, A[1]}), .B(B), .C(n4b_mod2_divider_4_c));  // open: D
  _4b_mod2_divider u_4b_mod2_divider_5 (.A({n4b_mod2_divider_4_c, A[0]}), .B(B), .C(n4b_mod2_divider_5_c));  // open: D
  _4b_mod2_divider u_4b_mod2_divider_6 (.A({n4b_mod2_divider_5_c, 1'b0}), .B(B), .C(n4b_mod2_divider_6_c));  // open: D
  _4b_mod2_divider u_4b_mod2_divider_7 (.A({n4b_mod2_divider_6_c, 1'b0}), .B(B), .C(n4b_mod2_divider_7_c));  // open: D
  _4b_mod2_divider u_4b_mod2_divider_8 (.A({n4b_mod2_divider_7_c, 1'b0}), .B(B), .C(Mod));  // open: D
endmodule
