// Logisim project FSM_713_9.circ as structural Verilog: 5 circuits, main circuit main
module main (
  output CLR,
  output [1:0] In,
  output Z,
  output halt
);

  wire clock_1_out;
  wire [3:3] rom_1_data;
  wire [7:0] counter_1_q;

  Clock clock_1 (.out(clock_1_out));
  Counter counter_1 (.Q(counter_1_q), .carry(halt), .clk(clock_1_out));  // open: load, D, count, clr
  ROM #(.dataWidth(4)) rom_1 (.addr(counter_1_q), .data({rom_1_data[3], In, CLR}));  // open: sel
  fsm fsm_1 (.In(In), .CLR(CLR), .Z(Z));
endmodule

module fsm (
  input  [1:0] In,
  input  CLR,
  output Z
);

  wire [1:0] state_store_1_s_2, state_trans_1_s1;

  state_trans state_trans_1 (.S(state_store_1_s_2), .In(In), .S1(state_trans_1_s1));
  state_store state_store_1 (.S(state_trans_1_s1), .CLR(CLR), .S_2(state_store_1_s_2));
  \output  output_1 (.In(In), .S(state_store_1_s_2), .Z(Z));
endmodule

module state_trans (
  input  [1:0] S,
  input  [1:0] In,
  output [1:0] S1
);

  wire and_1_out, and_2_out, and_3_out, and_4_out, not_1_out, not_2_out, not_3_out, not_4_out, not_5_out,
       not_6_out, not_7_out;

  not not_1 (not_1_out, S[1]);
  not not_2 (not_2_out, In[0]);
  not not_3 (not_3_out, S[0]);
  not not_4 (not_4_out, In[0]);
  not not_5 (not_5_out, In[1]);
  not not_6 (not_6_out, S[0]);
  not not_7 (not_7_out, In[0]);
  and and_1 (and_1_out, not_1_out, S[0], not_2_out);
  and and_2 (and_2_out, S[1], not_3_out, not_4_out);
  and and_3 (and_3_out, not_5_out, In[0]);
  and and_4 (and_4_out, S[1], not_6_out, not_7_out);
  or or_1 (S1[1], and_1_out, and_2_out);
  or or_2 (S1[0], and_3_out, and_4_out);
endmodule

module state_store (
  input  [1:0] S,
  input  CLR,
  output [1:0] S_2
);

  wire clock_1_out;
  wire [1:0] multiplexer_1_out;

  Multiplexer #(.width(2)) multiplexer_1 (.in0(S), .in1(2'b00), .out(multiplexer_1_out), .sel(CLR));  // open: en
  Register #(.width(2)) register_1 (.D(multiplexer_1_out), .Q(S_2), .clk(clock_1_out));  // open: en, clr
  Clock clock_1 (.out(clock_1_out));
endmodule

module \output  (
  input  [1:0] In,
  input  [1:0] S,
  output Z
);

  wire and_1_out;

  and and_1 (and_1_out, ~S[0], S[1]);  // AND_Gate
  and and_2 (Z, ~In[0], and_1_out);  // AND_Gate
endmodule
