// Logisim project GRF_713_269.circ as structural Verilog
module grf (
  input  clk,
  input  reset,
  input  [31:0] WD,
  input  [4:0] A3,
  input  [4:0] A1,
  input  WE,
  input  [4:0] A2,
  output [31:0] RD1,
  output [31:0] RD2
);

  wire En_00, En_01, En_02, En_03, En_04, En_05, En_06, En_07, En_08, En_09, En_10, En_11, En_12, En_13,
       En_14, En_15, En_16, En_17, En_18, En_19, En_20, En_21, En_22, En_23, En_24, En_25, En_26, En_27,
       En_28, En_29, En_30, En_31;
  wire [31:0] In_01, In_02, In_03, In_04, In_05, In_06, In_07, In_08, In_09, In_10, In_11, In_12, In_13,
       In_14, In_15, In_16, In_17, In_18, In_19, In_20, In_21, In_22, In_23, In_24, In_25, In_26, In_27,
       In_28, In_29, In_30, In_31, Out_00, Out_01, Out_02, Out_03, Out_04, Out_05, Out_06, Out_07, Out_08,
       Out_09, Out_10, Out_11, Out_12, Out_13, Out_14, Out_15, Out_16, Out_17, Out_18, Out_19, Out_20,
       Out_21, Out_22, Out_23, Out_24, Out_25, Out_26, Out_27, Out_28, Out_29, Out_30, Out_31;

  Demultiplexer #(.select(5), .width(32), .disabled(0), .enable("false")) demultiplexer_1 (
    .out1(In_01), .out2(In_02), .out3(In_03), .out4(In_04), .out5(In_05), .out6(In_06), .out7(In_07),
    .out8(In_08), .out9(In_09), .out10(In_10), .out11(In_11), .out12(In_12), .out13(In_13), .out14(In_14),
    .out15(In_15), .out16(In_16), .out17(In_17), .out18(In_18), .out19(In_19), .out20(In_20), .out21(In_21),
    .out22(In_22), .out23(In_23), .out24(In_24), .out25(In_25), .out26(In_26), .out27(In_27), .out28(In_28),
    .out29(In_29), .out30(In_30), .out31(In_31), .in(WD), .sel(A3));  // open: out0
  Demultiplexer #(.select(5), .disabled(0), .enable("false")) demultiplexer_2 (
    .out0(En_00), .out1(En_01), .out2(En_02), .out3(En_03), .out4(En_04), .out5(En_05), .out6(En_06),
    .out7(En_07), .out8(En_08), .out9(En_09), .out10(En_10), .out11(En_11), .out12(En_12), .out13(En_13),
    .out14(En_14), .out15(En_15), .out16(En_16), .out17(En_17), .out18(En_18), .out19(En_19), .out20(En_20),
    .out21(En_21), .out22(En_22), .out23(En_23), .out24(En_24), .out25(En_25), .out26(En_26), .out27(En_27),
    .out28(En_28), .out29(En_29), .out30(En_30), .out31(En_31), .in(WE), .sel(A3));
  Register #(.width(32)) register_1 (.D({32{1'b0}}), .en(En_00), .Q(Out_00), .clk(clk), .clr(reset));
  Register #(.width(32)) register_2 (.D(In_08), .en(En_08), .Q(Out_08), .clk(clk), .clr(reset));
  Register #(.width(32)) register_3 (.D(In_16), .en(En_16), .Q(Out_16), .clk(clk), .clr(reset));
  Register #(.width(32)) register_4 (.D(In_24), .en(En_24), .Q(Out_24), .clk(clk), .clr(reset));
  Register #(.width(32)) register_5 (.D(In_01), .en(En_01), .Q(Out_01), .clk(clk), .clr(reset));
  Register #(.width(32)) register_6 (.D(In_09), .en(En_09), .Q(Out_09), .clk(clk), .clr(reset));
  Register #(.width(32)) register_7 (.D(In_17), .en(En_17), .Q(Out_17), .clk(clk), .clr(reset));
  Register #(.width(32)) register_8 (.D(In_25), .en(En_25), .Q(Out_25), .clk(clk), .clr(reset));
  Register #(.width(32)) register_9 (.D(In_02), .en(En_02), .Q(Out_02), .clk(clk), .clr(reset));
  Register #(.width(32)) register_10 (.D(In_10), .en(En_10), .Q(Out_10), .clk(clk), .clr(reset));
  Register #(.width(32)) register_11 (.D(In_18), .en(En_18), .Q(Out_18), .clk(clk), .clr(reset));
  Register #(.width(32)) register_12 (.D(In_26), .en(En_26), .Q(Out_26), .clk(clk), .clr(reset));
  Register #(.width(32)) register_13 (.D(In_03), .en(En_03), .Q(Out_03), .clk(clk), .clr(reset));
  Register #(.width(32)) register_14 (.D(In_11), .en(En_11), .Q(Out_11), .clk(clk), .clr(reset));
  Register #(.width(32)) register_15 (.D(In_19), .en(En_19), .Q(Out_19), .clk(clk), .clr(reset));
  Register #(.width(32)) register_16 (.D(In_27), .en(En_27), .Q(Out_27), .clk(clk), .clr(reset));
  Register #(.width(32)) register_17 (.D(In_04), .en(En_04), .Q(Out_04), .clk(clk), .clr(reset));
  Register #(.width(32)) register_18 (.D(In_12), .en(En_12), .Q(Out_12), .clk(clk), .clr(reset));
  Register #(.width(32)) register_19 (.D(In_20), .en(En_20), .Q(Out_20), .clk(clk), .clr(reset));
  Register #(.width(32)) register_20 (.D(In_28), .en(En_28), .Q(Out_28), .clk(clk), .clr(reset));
  Multiplexer #(.select(5), .width(32), .disabled(0), .enable("false")) multiplexer_1 (
    .in0(Out_00), .in1(Out_01), .in2(Out_02), .in3(Out_03), .in4(Out_04), .in5(Out_05), .in6(Out_06),
    .in7(Out_07), .in8(Out_08), .in9(Out_09), .in10(Out_10), .in11(Out_11), .in12(Out_12), .in13(Out_13),
    .in14(Out_14), .in15(Out_15), .in16(Out_16), .in17(Out_17), .in18(Out_18), .in19(Out_19), .in20(Out_20),
    .in21(Out_21), .in22(Out_22), .in23(Out_23), .in24(Out_24), .in25(Out_25), .in26(Out_26), .in27(Out_27),
    .in28(Out_28), .in29(Out_29), .in30(Out_30), .in31(Out_31), .out(RD1), .sel(A1));
  Multiplexer #(.select(5), .width(32), .disabled(0), .enable("false")) multiplexer_2 (
    .in0(Out_00), .in1(Out_01), .in2(Out_02), .in3(Out_03), .in4(Out_04), .in5(Out_05), .in6(Out_06),
    .in7(Out_07), .in8(Out_08), .in9(Out_09), .in10(Out_10), .in11(Out_11), .in12(Out_12), .in13(Out_13),
    .in14(Out_14), .in15(Out_15), .in16(Out_16), .in17(Out_17), .in18(Out_18), .in19(Out_19), .in20(Out_20),
    .in21(Out_21), .in22(Out_22), .in23(Out_23), .in24(Out_24), .in25(Out_25), .in26(Out_26), .in27(Out_27),
    .in28(Out_28), .in29(Out_29), .in30(Out_30), .in31(Out_31), .out(RD2), .sel(A2));
  Register #(.width(32)) register_21 (.D(In_05), .en(En_05), .Q(Out_05), .clk(clk), .clr(reset));
  Register #(.width(32)) register_22 (.D(In_13), .en(En_13), .Q(Out_13), .clk(clk), .clr(reset));
  Register #(.width(32)) register_23 (.D(In_21), .en(En_21), .Q(Out_21), .clk(clk), .clr(reset));
  Register #(.width(32)) register_24 (.D(In_29), .en(En_29), .Q(Out_29), .clk(clk), .clr(reset));
  Register #(.width(32)) register_25 (.D(In_06), .en(En_06), .Q(Out_06), .clk(clk), .clr(reset));
  Register #(.width(32)) register_26 (.D(In_14), .en(En_14), .Q(Out_14), .clk(clk), .clr(reset));
  Register #(.width(32)) register_27 (.D(In_22), .en(En_22), .Q(Out_22), .clk(clk), .clr(reset));
  Register #(.width(32)) register_28 (.D(In_30), .en(En_30), .Q(Out_30), .clk(clk), .clr(reset));
  Register #(.width(32)) register_29 (.D(In_07), .en(En_07), .Q(Out_07), .clk(clk), .clr(reset));
  Register #(.width(32)) register_30 (.D(In_15), .en(En_15), .Q(Out_15), .clk(clk), .clr(reset));
  Register #(.width(32)) register_31 (.D(In_23), .en(En_23), .Q(Out_23), .clk(clk), .clr(reset));
  Register #(.width(32)) register_32 (.D(In_31), .en(En_31), .Q(Out_31), .clk(clk), .clr(reset));

  // Other names for the same wires on the sheet: Re = reset
endmodule
