// Logisim project GRF_713_269_2.circ as structural Verilog
module reg2_file (
  input  [31:0] WD,
  input  A3,
  input  A1,
  input  En,
  input  A2,
  input  Clk,
  input  Clr,
  output [31:0] RD1,
  output [31:0] RD2
);

  wire demultiplexer_2_out0, demultiplexer_2_out1;
  wire [31:0] demultiplexer_1_out0, demultiplexer_1_out1, register_1_q, register_2_q;

  Demultiplexer #(.width(32), .disabled(0), .enable("false")) demultiplexer_1 (
    .out0(demultiplexer_1_out0), .out1(demultiplexer_1_out1), .in(WD), .sel(A3));
  Demultiplexer #(.disabled(0), .enable("false")) demultiplexer_2 (
    .out0(demultiplexer_2_out0), .out1(demultiplexer_2_out1), .in(En), .sel(A3));
  Register #(.width(32)) register_1 (
    .D(demultiplexer_1_out0), .en(demultiplexer_2_out0), .Q(register_1_q), .clk(Clk), .clr(Clr));
  Register #(.width(32)) register_2 (
    .D(demultiplexer_1_out1), .en(demultiplexer_2_out1), .Q(register_2_q), .clk(Clk), .clr(Clr));
  Multiplexer #(.width(32), .disabled(0), .enable("false")) multiplexer_1 (
    .in0(register_1_q), .in1(register_2_q), .out(RD1), .sel(A1));
  Multiplexer #(.width(32), .disabled(0), .enable("false")) multiplexer_2 (
    .in0(register_1_q), .in1(register_2_q), .out(RD2), .sel(A2));
endmodule

module reg4_file (
  input  Clk,
  input  Clr,
  input  WE,
  input  [31:0] WD,
  input  [1:0] A3,
  input  [1:0] A1,
  input  [1:0] A2,
  output [31:0] RD1,
  output [31:0] RD2
);

  wire demultiplexer_1_out0, demultiplexer_1_out1;
  wire [31:0] demultiplexer_2_out0, demultiplexer_2_out1, reg2_file_1_rd1, reg2_file_1_rd2, reg2_file_2_rd1,
       reg2_file_2_rd2;

  Demultiplexer #(.disabled(0), .enable("false")) demultiplexer_1 (
    .out0(demultiplexer_1_out0), .out1(demultiplexer_1_out1), .in(WE), .sel(A3[1]));
  Demultiplexer #(.width(32), .disabled(0), .enable("false")) demultiplexer_2 (
    .out0(demultiplexer_2_out0), .out1(demultiplexer_2_out1), .in(WD), .sel(A3[1]));
  reg2_file reg2_file_1 (
    .WD(demultiplexer_2_out0), .A3(A3[0]), .En(demultiplexer_1_out0), .A1(A1[0]), .Clk(Clk), .A2(A2[0]),
    .Clr(Clr), .RD1(reg2_file_1_rd1), .RD2(reg2_file_1_rd2));
  reg2_file reg2_file_2 (
    .WD(demultiplexer_2_out1), .A3(A3[0]), .En(demultiplexer_1_out1), .A1(A1[0]), .Clk(Clk), .A2(A2[0]),
    .Clr(Clr), .RD1(reg2_file_2_rd1), .RD2(reg2_file_2_rd2));
  Multiplexer #(.width(32), .disabled(0), .enable("false")) multiplexer_1 (
    .in0(reg2_file_1_rd1), .in1(reg2_file_2_rd1), .out(RD1), .sel(A1[1]));
  Multiplexer #(.width(32), .disabled(0), .enable("false")) multiplexer_2 (
    .in0(reg2_file_1_rd2), .in1(reg2_file_2_rd2), .out(RD2), .sel(A2[1]));
endmodule

module reg8_file (
  input  Clk,
  input  Clr,
  input  WE,
  input  [31:0] WD,
  input  [2:0] A3,
  input  [2:0] A1,
  input  [2:0] A2,
  output [31:0] RD1,
  output [31:0] RD2
);

  wire demultiplexer_1_out0, demultiplexer_1_out1;
  wire [31:0] demultiplexer_2_out0, demultiplexer_2_out1, reg4_file_1_rd1, reg4_file_1_rd2, reg4_file_2_rd1,
       reg4_file_2_rd2;

  Demultiplexer #(.disabled(0), .enable("false")) demultiplexer_1 (
    .out0(demultiplexer_1_out0), .out1(demultiplexer_1_out1), .in(WE), .sel(A3[2]));
  Demultiplexer #(.width(32), .disabled(0), .enable("false")) demultiplexer_2 (
    .out0(demultiplexer_2_out0), .out1(demultiplexer_2_out1), .in(WD), .sel(A3[2]));
  reg4_file reg4_file_1 (
    .Clk(Clk), .Clr(Clr), .WE(demultiplexer_1_out0), .WD(demultiplexer_2_out0), .A3(A3[1:0]), .A1(A1[1:0]),
    .A2(A2[1:0]), .RD1(reg4_file_1_rd1), .RD2(reg4_file_1_rd2));
  reg4_file reg4_file_2 (
    .Clk(Clk), .Clr(Clr), .WE(demultiplexer_1_out1), .WD(demultiplexer_2_out1), .A3(A3[1:0]), .A1(A1[1:0]),
    .A2(A2[1:0]), .RD1(reg4_file_2_rd1), .RD2(reg4_file_2_rd2));
  Multiplexer #(.width(32), .disabled(0), .enable("false")) multiplexer_1 (
    .in0(reg4_file_1_rd1), .in1(reg4_file_2_rd1), .out(RD1), .sel(A1[2]));
  Multiplexer #(.width(32), .disabled(0), .enable("false")) multiplexer_2 (
    .in0(reg4_file_1_rd2), .in1(reg4_file_2_rd2), .out(RD2), .sel(A2[2]));
endmodule

module reg16_file (
  input  Clk,
  input  Clr,
  input  WE,
  input  [31:0] WD,
  input  [3:0] A3,
  input  [3:0] A1,
  input  [3:0] A2,
  output [31:0] RD1,
  output [31:0] RD2
);

  wire demultiplexer_1_out0, demultiplexer_1_out1;
  wire [31:0] demultiplexer_2_out0, demultiplexer_2_out1, reg8_file_1_rd1, reg8_file_1_rd2, reg8_file_2_rd1,
       reg8_file_2_rd2;

  Demultiplexer #(.disabled(0), .enable("false")) demultiplexer_1 (
    .out0(demultiplexer_1_out0), .out1(demultiplexer_1_out1), .in(WE), .sel(A3[3]));
  Demultiplexer #(.width(32), .disabled(0), .enable("false")) demultiplexer_2 (
    .out0(demultiplexer_2_out0), .out1(demultiplexer_2_out1), .in(WD), .sel(A3[3]));
  reg8_file reg8_file_1 (
    .Clk(Clk), .Clr(Clr), .WE(demultiplexer_1_out0), .WD(demultiplexer_2_out0), .A3(A3[2:0]), .A1(A1[2:0]),
    .A2(A2[2:0]), .RD1(reg8_file_1_rd1), .RD2(reg8_file_1_rd2));
  reg8_file reg8_file_2 (
    .Clk(Clk), .Clr(Clr), .WE(demultiplexer_1_out1), .WD(demultiplexer_2_out1), .A3(A3[2:0]), .A1(A1[2:0]),
    .A2(A2[2:0]), .RD1(reg8_file_2_rd1), .RD2(reg8_file_2_rd2));
  Multiplexer #(.width(32), .disabled(0), .enable("false")) multiplexer_1 (
    .in0(reg8_file_1_rd1), .in1(reg8_file_2_rd1), .out(RD1), .sel(A1[3]));
  Multiplexer #(.width(32), .disabled(0), .enable("false")) multiplexer_2 (
    .in0(reg8_file_1_rd2), .in1(reg8_file_2_rd2), .out(RD2), .sel(A2[3]));
endmodule

module reg32_file (
  input  Clk,
  input  Clr,
  input  WE,
  input  [31:0] WD,
  input  [4:0] A3,
  input  [4:0] A1,
  input  [4:0] A2,
  output [31:0] RD1,
  output [31:0] RD2
);

  wire demultiplexer_1_out0, demultiplexer_1_out1;
  wire [31:0] demultiplexer_2_out0, demultiplexer_2_out1, reg16_file_1_rd1, reg16_file_1_rd2,
       reg16_file_2_rd1, reg16_file_2_rd2;

  Demultiplexer #(.disabled(0), .enable("false")) demultiplexer_1 (
    .out0(demultiplexer_1_out0), .out1(demultiplexer_1_out1), .in(WE), .sel(A3[4]));
  Demultiplexer #(.width(32), .disabled(0), .enable("false")) demultiplexer_2 (
    .out0(demultiplexer_2_out0), .out1(demultiplexer_2_out1), .in(WD), .sel(A3[4]));
  reg16_file reg16_file_1 (
    .Clk(Clk), .Clr(Clr), .WE(demultiplexer_1_out0), .WD(demultiplexer_2_out0), .A3(A3[3:0]), .A1(A1[3:0]),
    .A2(A2[3:0]), .RD1(reg16_file_1_rd1), .RD2(reg16_file_1_rd2));
  reg16_file reg16_file_2 (
    .Clk(Clk), .Clr(Clr), .WE(demultiplexer_1_out1), .WD(demultiplexer_2_out1), .A3(A3[3:0]), .A1(A1[3:0]),
    .A2(A2[3:0]), .RD1(reg16_file_2_rd1), .RD2(reg16_file_2_rd2));
  Multiplexer #(.width(32), .disabled(0), .enable("false")) multiplexer_1 (
    .in0(reg16_file_1_rd1), .in1(reg16_file_2_rd1), .out(RD1), .sel(A1[4]));
  Multiplexer #(.width(32), .disabled(0), .enable("false")) multiplexer_2 (
    .in0(reg16_file_1_rd2), .in1(reg16_file_2_rd2), .out(RD2), .sel(A2[4]));
endmodule

module grf (
  input  WE,
  input  [4:0] A3,
  input  Clk,
  input  Clr,
  input  [4:0] A1,
  input  [4:0] A2,
  input  [31:0] WD,
  output [31:0] RD1,
  output [31:0] RD2
);

  wire comparator_1_eq, multiplexer_1_out;

  Comparator #(.width(5), .mode("unsigned")) comparator_1 (
    .a(A3), .b({5{1'b0}}), .eq(comparator_1_eq));  // open: gt, lt
  Multiplexer #(.disabled(0), .enable("false")) multiplexer_1 (
    .in0(WE), .in1(1'b0), .out(multiplexer_1_out), .sel(comparator_1_eq));
  reg32_file reg32_file_1 (
    .Clk(Clk), .Clr(Clr), .WE(multiplexer_1_out), .WD(WD), .A3(A3), .A1(A1), .A2(A2), .RD1(RD1), .RD2(RD2));
endmodule
