// Logisim project ftoi_713_319.circ as structural Verilog
module ftoi (
  input  [15:0] float,
  output [31:0] \int 
);

  wire comparator_2_eq, subtractor_1_bout;
  wire [4:0] not_1_out, subtractor_1_out;
  wire [10:10] comparator_1_gt;
  wire [15:0] multiplexer_1_out;
  wire [25:0] shifter_1_out;
  wire [31:0] multiplexer_2_out, negator_1_out;

  assign not_1_out = ~float[14:10];  // NOT_Gate not_1, 5 bits wide
  Comparator #(.width(5), .mode("unsigned")) comparator_1 (
    .a(float[14:10]), .b({5{1'b0}}), .gt(comparator_1_gt[10]));  // open: eq, lt
  Subtractor #(.width(5)) subtractor_1 (
    .a(float[14:10]), .b(5'b01111), .out(subtractor_1_out), .bout(subtractor_1_bout));  // open: bin
  Comparator #(.width(5), .mode("unsigned")) comparator_2 (
    .a(not_1_out), .b({5{1'b0}}), .eq(comparator_2_eq));  // open: gt, lt
  Shifter #(.width(26)) shifter_1 (
    .in({{15{1'b0}}, comparator_1_gt[10], float[9:0]}), .\dist (subtractor_1_out), .out(shifter_1_out));
  Multiplexer #(.width(16), .disabled(0), .enable("false")) multiplexer_1 (
    .in0(shifter_1_out[25:10]), .in1({16{1'b0}}), .out(multiplexer_1_out), .sel(subtractor_1_bout));
  Negator #(.width(32)) negator_1 (.in({{16{1'b0}}, multiplexer_1_out}), .out(negator_1_out));
  Multiplexer #(.width(32), .disabled(0), .enable("false")) multiplexer_2 (
    .in0({{16{1'b0}}, multiplexer_1_out}), .in1(negator_1_out), .out(multiplexer_2_out), .sel(float[15]));
  Multiplexer #(.width(32), .disabled(0), .enable("false")) multiplexer_3 (
    .in0(multiplexer_2_out), .in1({32{1'b0}}), .out(\int ), .sel(comparator_2_eq));
endmodule
