// Logisim project navigation_713_393.circ as structural Verilog
module state_trans (
  input  S3,
  input  S2,
  input  S1,
  input  S0,
  input  dir1,
  input  dir0,
  output S3_2,
  output S2_2,
  output S1_2,
  output S0_2
);

  wire and_1_out, and_2_out, and_3_out, and_4_out, and_5_out, and_6_out, and_7_out, and_8_out, and_9_out,
       and_10_out, and_11_out, and_12_out, and_13_out, and_14_out, and_15_out, and_16_out, not_1_out,
       not_2_out, not_3_out, not_4_out, not_5_out, not_6_out, not_7_out, not_8_out, not_9_out, not_10_out,
       not_11_out, not_12_out, not_13_out, not_14_out, not_15_out, not_16_out, not_17_out, not_18_out,
       not_19_out, not_20_out, not_21_out, not_22_out, not_23_out, not_24_out, not_25_out, not_26_out,
       not_27_out, not_28_out;

  not not_1 (not_1_out, S1);
  not not_2 (not_2_out, dir1);
  not not_3 (not_3_out, dir0);
  not not_4 (not_4_out, dir1);
  not not_5 (not_5_out, S2);
  not not_6 (not_6_out, dir1);
  not not_7 (not_7_out, dir1);
  not not_8 (not_8_out, dir0);
  not not_9 (not_9_out, S1);
  not not_10 (not_10_out, dir1);
  not not_11 (not_11_out, S1);
  not not_12 (not_12_out, dir0);
  not not_13 (not_13_out, S3);
  not not_14 (not_14_out, S2);
  not not_15 (not_15_out, dir1);
  not not_16 (not_16_out, dir0);
  not not_17 (not_17_out, dir0);
  not not_18 (not_18_out, S3);
  not not_19 (not_19_out, S1);
  not not_20 (not_20_out, dir1);
  not not_21 (not_21_out, S3);
  not not_22 (not_22_out, S2);
  not not_23 (not_23_out, S1);
  not not_24 (not_24_out, S3);
  not not_25 (not_25_out, S1);
  not not_26 (not_26_out, dir0);
  not not_27 (not_27_out, dir1);
  not not_28 (not_28_out, dir0);
  and and_1 (and_1_out, S2, not_1_out, not_2_out, not_3_out);
  and and_2 (and_2_out, S2, S1, not_4_out, dir0);
  and and_3 (and_3_out, not_5_out, S1, not_6_out);
  and and_4 (and_4_out, S1, not_7_out, not_8_out);
  and and_5 (and_5_out, S2, not_9_out, not_10_out, dir0);
  and and_6 (and_6_out, S2, not_11_out, dir1, not_12_out);
  and and_7 (and_7_out, S2, S1, dir1, dir0);
  and and_8 (and_8_out, not_13_out, not_14_out, not_15_out, not_16_out);
  and and_9 (and_9_out, S1, dir1, dir0);
  and and_10 (and_10_out, S2, dir1, dir0);
  and and_11 (and_11_out, S2, S1, not_17_out);
  and and_12 (and_12_out, not_18_out, not_19_out, not_20_out, dir0);
  and and_13 (and_13_out, not_21_out, not_22_out, not_23_out, dir1);
  and and_14 (and_14_out, not_24_out, not_25_out, dir1, not_26_out);
  and and_15 (and_15_out, S1, dir1, dir0);
  and and_16 (and_16_out, S2, S1, not_27_out, not_28_out);
  or or_1 (S3_2, and_1_out, and_2_out);
  or or_2 (S2_2, and_3_out, and_4_out, and_5_out, and_6_out, and_7_out);
  or or_3 (S1_2, and_8_out, and_9_out, and_10_out, and_11_out);
  or or_4 (S0_2, and_12_out, and_13_out, and_14_out, and_15_out, and_16_out);
endmodule

module navigation (
  input  [1:0] dir,
  input  clk,
  input  reset,
  output arrive,
  output hit
);

  wire [2:1] register_1_q;
  wire [3:0] state_trans_1_s3_2;

  state_trans state_trans_1 (
    .S3(arrive), .S2(register_1_q[1]), .S3_2(state_trans_1_s3_2[0]), .S1(register_1_q[2]), .S0(hit),
    .dir1(dir[1]), .dir0(dir[0]), .S2_2(state_trans_1_s3_2[1]), .S1_2(state_trans_1_s3_2[2]),
    .S0_2(state_trans_1_s3_2[3]));
  Register #(.width(4)) register_1 (
    .D(state_trans_1_s3_2), .Q({hit, register_1_q, arrive}), .clk(clk), .clr(reset));  // open: en
endmodule
