// Logisim project scmCPU.circ as structural Verilog: 10 circuits, main circuit test
module test (
  output [31:0] Instr,
  output RegWrite,
  output [4:0] RegAddr,
  output [31:0] RegData,
  output MemWrite,
  output halt,
  output [4:0] MemAddr,
  output [31:0] MemData
);

  wire clock_1_out, comparator_1_gt;
  wire [31:0] counter_1_q;

  Clock clock_1 (.out(clock_1_out));
  Counter #(.width(32), .max('hffffffff), .ongoal("stay")) counter_1 (
    .Q(counter_1_q), .carry(halt), .clk(clock_1_out));  // open: load, D, count, clr
  Comparator #(.width(32), .mode("unsigned")) comparator_1 (
    .a(32'h4), .b(counter_1_q), .gt(comparator_1_gt));  // open: eq, lt
  main main_1 (
    .in_1(comparator_1_gt), .Instr(Instr), .RegWrite(RegWrite), .RegAddr(RegAddr), .RegData(RegData),
    .MemWrite(MemWrite), .MemAddr(MemAddr), .MemData(MemData));
endmodule

// CPU
module main (
  input  in_1,
  output [31:0] Instr,
  output RegWrite,
  output [4:0] RegAddr,
  output [31:0] RegData,
  output MemWrite,
  output [4:0] MemAddr,
  output [31:0] MemData
);

  wire alu_1_flag, ALUSrc, Clk, EXTCtrl;
  wire [1:0] DataToReg, DMCtrl, RegDst;
  wire [2:0] NPCCtrl;
  wire [3:0] ALUCtrl;
  wire [31:0] alu_1_out, dm_1_rd, ext_1_out32, grf_1_rd1, multiplexer_2_out, npc_1_nextpc, npc_1_pcadd4,
       pc_1_pc;

  Clock clock_1 (.out(Clk));
  PC pc_1 (.NextPC(npc_1_nextpc), .Clk(Clk), .Rst(in_1), .PC(pc_1_pc));
  NPC npc_1 (
    .Ctrl(NPCCtrl), .PC(pc_1_pc), .Offset(Instr[15:0]), .Index(Instr[25:0]), .NextPC(npc_1_nextpc),
    .BrFlag(alu_1_flag), .Reg(grf_1_rd1), .PCAdd4(npc_1_pcadd4));
  IM im_1 (.A(pc_1_pc[6:2]), .RD(Instr));
  Controller controller_1 (
    .Op(Instr[31:26]), .Funct(Instr[5:0]), .RegDst(RegDst), .RegWrite(RegWrite), .ALUSrc(ALUSrc),
    .MemWrite(MemWrite), .DataToReg(DataToReg), .NPCCtrl(NPCCtrl), .ALUCtrl(ALUCtrl), .EXTCtrl(EXTCtrl),
    .DMCtrl(DMCtrl));
  Multiplexer #(.select(2), .width(5), .disabled(0), .enable("false")) multiplexer_1 (
    .in0(Instr[20:16]), .in1(Instr[15:11]), .in2({5{1'b1}}), .out(RegAddr), .sel(RegDst));  // open: in3
  GRF grf_1 (
    .Clk(Clk), .Rst(in_1), .WD(RegData), .A3(RegAddr), .A1(Instr[25:21]), .WE(RegWrite), .A2(Instr[20:16]),
    .RD1(grf_1_rd1), .RD2(MemData));
  EXT ext_1 (.In16(Instr[15:0]), .Out32(ext_1_out32), .Ctrl(EXTCtrl));
  Multiplexer #(.width(32), .disabled(0), .enable("false")) multiplexer_2 (
    .in0(MemData), .in1(ext_1_out32), .out(multiplexer_2_out), .sel(ALUSrc));
  ALU alu_1 (
    .SrcA(grf_1_rd1), .SrcB(multiplexer_2_out), .Ctrl(ALUCtrl),
    .Out({alu_1_out[31:7], MemAddr, alu_1_out[1:0]}), .Flag(alu_1_flag), .Shamt(Instr[10:6]));
  DM dm_1 (
    .A(MemAddr), .WD(MemData), .WE(MemWrite), .Clk(Clk), .Rst(in_1), .RD(dm_1_rd), .ByteSel(alu_1_out[1:0]),
    .Ctrl(DMCtrl));
  Multiplexer #(.select(2), .width(32), .disabled(0), .enable("false")) multiplexer_3 (
    .in0({alu_1_out[31:7], MemAddr, alu_1_out[1:0]}), .in1(dm_1_rd), .in2(npc_1_pcadd4), .out(RegData),
    .sel(DataToReg));  // open: in3

  // Other names for the same wires on the sheet: Rst = in_1
endmodule

module PC (
  input  [31:0] NextPC,
  input  Clk,
  input  Rst,
  output [31:0] PC
);

  Register #(.width(32)) register_1 (.D(NextPC), .Q(PC), .clk(Clk), .clr(Rst));  // open: en
endmodule

module IM (
  input  [4:0] A,
  output [31:0] RD
);

  ROM #(.addrWidth(5), .dataWidth(32)) rom_1 (.addr(A), .data(RD));  // open: sel

  // Notes on the sheet:
  //   contents of rom_1 (hex, n*v repeats v):
  //   34840001 34a50002 c000c04 1000000d a4040000 a4050002 a0040004 a0050005 a0040006 a0050007 84080000
  //   84090002 800a0004 800b0005 800c0006 800d0007 3e00008
endmodule

module DM (
  input  [31:0] WD,
  input  [1:0] ByteSel,
  input  [1:0] Ctrl,
  input  [4:0] A,
  input  WE,
  input  Clk,
  input  Rst,
  output [31:0] RD
);

  wire [7:0] _0_7, multiplexer_4_out;
  wire [15:0] multiplexer_3_out;
  wire [15:8] _0_15;
  wire [31:0] bit_extender_1_out, bit_extender_2_out, Byte, HalfWord, multiplexer_1_out;
  wire [31:16] _0_31;

  Multiplexer #(.select(2), .width(32), .disabled(0), .enable("false")) multiplexer_1 (
    .in0(WD), .in1(HalfWord), .in2(Byte), .out(multiplexer_1_out), .sel(Ctrl));  // open: in3
  Multiplexer #(.width(32), .disabled(0), .enable("false")) multiplexer_2 (
    .in0({_0_31, WD[15:0]}), .in1({WD[15:0], _0_15, _0_7}), .out(HalfWord), .sel(ByteSel[1]));
  RAM #(.addrWidth(5), .dataWidth(32), .bus("separate")) ram_1 (
    .addr(A), .din(multiplexer_1_out), .data({_0_31, _0_15, _0_7}), .str(WE), .clk(Clk), .clr(Rst));  // open: sel, ld
  Multiplexer #(.width(16), .disabled(0), .enable("false")) multiplexer_3 (
    .in0({_0_15, _0_7}), .in1(_0_31), .out(multiplexer_3_out), .sel(ByteSel[1]));
  Multiplexer #(.select(2), .width(8), .disabled(0), .enable("false")) multiplexer_4 (
    .in0(_0_7), .in1(_0_15), .in2(_0_31[23:16]), .in3(_0_31[31:24]), .out(multiplexer_4_out), .sel(ByteSel));
  Multiplexer #(.select(2), .width(32), .disabled(0), .enable("false")) multiplexer_5 (
    .in0({_0_31, _0_15, WD[7:0]}), .in1({_0_31, WD[7:0], _0_7}), .in2({_0_31[31:24], WD[7:0], _0_15, _0_7}),
    .in3({WD[7:0], _0_31[23:16], _0_15, _0_7}), .out(Byte), .sel(ByteSel));
  assign bit_extender_1_out = {{16{multiplexer_3_out[15]}}, multiplexer_3_out};  // Bit_Extender bit_extender_1
  assign bit_extender_2_out = {{24{multiplexer_4_out[7]}}, multiplexer_4_out};  // Bit_Extender bit_extender_2
  Multiplexer #(.select(2), .width(32), .disabled(0), .enable("false")) multiplexer_6 (
    .in0({_0_31, _0_15, _0_7}), .in1(bit_extender_1_out), .in2(bit_extender_2_out), .out(RD), .sel(Ctrl));  // open: in3

  // Other names for the same wires on the sheet: Word[31:0] = WD; _16_31[15:0] = _0_31; _24_31[7:0] = _0_31[31:24];
  //   _0_15[7:0] = _0_7; _0_31[15:0] = {_0_15, _0_7}; _8_15[7:0] = _0_15; _16_23[7:0] = _0_31[23:16];
  //   HalfSel = ByteSel[1]
endmodule

module GRF (
  input  Clk,
  input  Rst,
  input  [31:0] WD,
  input  [4:0] A3,
  input  [4:0] A1,
  input  WE,
  input  [4:0] A2,
  output [31:0] RD1,
  output [31:0] RD2
);

  wire En_00, En_01, En_02, En_03, En_04, En_05, En_06, En_07, En_08, En_09, En_10, En_11, En_12, En_13,
       En_14, En_15, En_16, En_17, En_18, En_19, En_20, En_21, En_22, En_23, En_24, En_25, En_26, En_27,
       En_28, En_29, En_30, En_31;
  wire [31:0] In_01, In_02, In_03, In_04, In_05, In_06, In_07, In_08, In_09, In_10, In_11, In_12, In_13,
       In_14, In_15, In_16, In_17, In_18, In_19, In_20, In_21, In_22, In_23, In_24, In_25, In_26, In_27,
       In_28, In_29, In_30, In_31, Out_00, Out_01, Out_02, Out_03, Out_04, Out_05, Out_06, Out_07, Out_08,
       Out_09, Out_10, Out_11, Out_12, Out_13, Out_14, Out_15, Out_16, Out_17, Out_18, Out_19, Out_20,
       Out_21, Out_22, Out_23, Out_24, Out_25, Out_26, Out_27, Out_28, Out_29, Out_30, Out_31;

  Demultiplexer #(.select(5), .width(32), .disabled(0), .enable("false")) demultiplexer_1 (
    .out1(In_01), .out2(In_02), .out3(In_03), .out4(In_04), .out5(In_05), .out6(In_06), .out7(In_07),
    .out8(In_08), .out9(In_09), .out10(In_10), .out11(In_11), .out12(In_12), .out13(In_13), .out14(In_14),
    .out15(In_15), .out16(In_16), .out17(In_17), .out18(In_18), .out19(In_19), .out20(In_20), .out21(In_21),
    .out22(In_22), .out23(In_23), .out24(In_24), .out25(In_25), .out26(In_26), .out27(In_27), .out28(In_28),
    .out29(In_29), .out30(In_30), .out31(In_31), .in(WD), .sel(A3));  // open: out0
  Demultiplexer #(.select(5), .disabled(0), .enable("false")) demultiplexer_2 (
    .out0(En_00), .out1(En_01), .out2(En_02), .out3(En_03), .out4(En_04), .out5(En_05), .out6(En_06),
    .out7(En_07), .out8(En_08), .out9(En_09), .out10(En_10), .out11(En_11), .out12(En_12), .out13(En_13),
    .out14(En_14), .out15(En_15), .out16(En_16), .out17(En_17), .out18(En_18), .out19(En_19), .out20(En_20),
    .out21(En_21), .out22(En_22), .out23(En_23), .out24(En_24), .out25(En_25), .out26(En_26), .out27(En_27),
    .out28(En_28), .out29(En_29), .out30(En_30), .out31(En_31), .in(WE), .sel(A3));
  Register #(.width(32)) register_1 (.D({32{1'b0}}), .en(En_00), .Q(Out_00), .clk(Clk), .clr(Rst));
  Register #(.width(32)) register_2 (.D(In_08), .en(En_08), .Q(Out_08), .clk(Clk), .clr(Rst));
  Register #(.width(32)) register_3 (.D(In_16), .en(En_16), .Q(Out_16), .clk(Clk), .clr(Rst));
  Register #(.width(32)) register_4 (.D(In_24), .en(En_24), .Q(Out_24), .clk(Clk), .clr(Rst));
  Register #(.width(32)) register_5 (.D(In_01), .en(En_01), .Q(Out_01), .clk(Clk), .clr(Rst));
  Register #(.width(32)) register_6 (.D(In_09), .en(En_09), .Q(Out_09), .clk(Clk), .clr(Rst));
  Register #(.width(32)) register_7 (.D(In_17), .en(En_17), .Q(Out_17), .clk(Clk), .clr(Rst));
  Register #(.width(32)) register_8 (.D(In_25), .en(En_25), .Q(Out_25), .clk(Clk), .clr(Rst));
  Register #(.width(32)) register_9 (.D(In_02), .en(En_02), .Q(Out_02), .clk(Clk), .clr(Rst));
  Register #(.width(32)) register_10 (.D(In_10), .en(En_10), .Q(Out_10), .clk(Clk), .clr(Rst));
  Register #(.width(32)) register_11 (.D(In_18), .en(En_18), .Q(Out_18), .clk(Clk), .clr(Rst));
  Register #(.width(32)) register_12 (.D(In_26), .en(En_26), .Q(Out_26), .clk(Clk), .clr(Rst));
  Register #(.width(32)) register_13 (.D(In_03), .en(En_03), .Q(Out_03), .clk(Clk), .clr(Rst));
  Register #(.width(32)) register_14 (.D(In_11), .en(En_11), .Q(Out_11), .clk(Clk), .clr(Rst));
  Register #(.width(32)) register_15 (.D(In_19), .en(En_19), .Q(Out_19), .clk(Clk), .clr(Rst));
  Register #(.width(32)) register_16 (.D(In_27), .en(En_27), .Q(Out_27), .clk(Clk), .clr(Rst));
  Register #(.width(32)) register_17 (.D(In_04), .en(En_04), .Q(Out_04), .clk(Clk), .clr(Rst));
  Register #(.width(32)) register_18 (.D(In_12), .en(En_12), .Q(Out_12), .clk(Clk), .clr(Rst));
  Register #(.width(32)) register_19 (.D(In_20), .en(En_20), .Q(Out_20), .clk(Clk), .clr(Rst));
  Register #(.width(32)) register_20 (.D(In_28), .en(En_28), .Q(Out_28), .clk(Clk), .clr(Rst));
  Multiplexer #(.select(5), .width(32), .disabled(0), .enable("false")) multiplexer_1 (
    .in0(Out_00), .in1(Out_01), .in2(Out_02), .in3(Out_03), .in4(Out_04), .in5(Out_05), .in6(Out_06),
    .in7(Out_07), .in8(Out_08), .in9(Out_09), .in10(Out_10), .in11(Out_11), .in12(Out_12), .in13(Out_13),
    .in14(Out_14), .in15(Out_15), .in16(Out_16), .in17(Out_17), .in18(Out_18), .in19(Out_19), .in20(Out_20),
    .in21(Out_21), .in22(Out_22), .in23(Out_23), .in24(Out_24), .in25(Out_25), .in26(Out_26), .in27(Out_27),
    .in28(Out_28), .in29(Out_29), .in30(Out_30), .in31(Out_31), .out(RD1), .sel(A1));
  Multiplexer #(.select(5), .width(32), .disabled(0), .enable("false")) multiplexer_2 (
    .in0(Out_00), .in1(Out_01), .in2(Out_02), .in3(Out_03), .in4(Out_04), .in5(Out_05), .in6(Out_06),
    .in7(Out_07), .in8(Out_08), .in9(Out_09), .in10(Out_10), .in11(Out_11), .in12(Out_12), .in13(Out_13),
    .in14(Out_14), .in15(Out_15), .in16(Out_16), .in17(Out_17), .in18(Out_18), .in19(Out_19), .in20(Out_20),
    .in21(Out_21), .in22(Out_22), .in23(Out_23), .in24(Out_24), .in25(Out_25), .in26(Out_26), .in27(Out_27),
    .in28(Out_28), .in29(Out_29), .in30(Out_30), .in31(Out_31), .out(RD2), .sel(A2));
  Register #(.width(32)) register_21 (.D(In_05), .en(En_05), .Q(Out_05), .clk(Clk), .clr(Rst));
  Register #(.width(32)) register_22 (.D(In_13), .en(En_13), .Q(Out_13), .clk(Clk), .clr(Rst));
  Register #(.width(32)) register_23 (.D(In_21), .en(En_21), .Q(Out_21), .clk(Clk), .clr(Rst));
  Register #(.width(32)) register_24 (.D(In_29), .en(En_29), .Q(Out_29), .clk(Clk), .clr(Rst));
  Register #(.width(32)) register_25 (.D(In_06), .en(En_06), .Q(Out_06), .clk(Clk), .clr(Rst));
  Register #(.width(32)) register_26 (.D(In_14), .en(En_14), .Q(Out_14), .clk(Clk), .clr(Rst));
  Register #(.width(32)) register_27 (.D(In_22), .en(En_22), .Q(Out_22), .clk(Clk), .clr(Rst));
  Register #(.width(32)) register_28 (.D(In_30), .en(En_30), .Q(Out_30), .clk(Clk), .clr(Rst));
  Register #(.width(32)) register_29 (.D(In_07), .en(En_07), .Q(Out_07), .clk(Clk), .clr(Rst));
  Register #(.width(32)) register_30 (.D(In_15), .en(En_15), .Q(Out_15), .clk(Clk), .clr(Rst));
  Register #(.width(32)) register_31 (.D(In_23), .en(En_23), .Q(Out_23), .clk(Clk), .clr(Rst));
  Register #(.width(32)) register_32 (.D(In_31), .en(En_31), .Q(Out_31), .clk(Clk), .clr(Rst));

  // Other names for the same wires on the sheet: Re = Rst
endmodule

module EXT (
  input  [15:0] In16,
  input  Ctrl,
  output [31:0] Out32
);

  wire [31:0] bit_extender_1_out, bit_extender_2_out;

  assign bit_extender_1_out = {{16{1'b0}}, In16};  // Bit_Extender bit_extender_1
  Multiplexer #(.width(32), .disabled(0), .enable("false")) multiplexer_1 (
    .in0(bit_extender_1_out), .in1(bit_extender_2_out), .out(Out32), .sel(Ctrl));
  assign bit_extender_2_out = {{16{In16[15]}}, In16};  // Bit_Extender bit_extender_2

  // Notes on the sheet:
  //   Ctrl: pull=down
endmodule

module ALU (
  input  [31:0] SrcA,
  input  [31:0] SrcB,
  input  [4:0] Shamt,
  input  [3:0] Ctrl,
  output [31:0] Out,
  output Flag
);

  wire eq, gt, gtu, lt, ltu;
  wire [31:0] add, \and , AsubB, bit_extender_1_out, BsubA, \or , sll, sllv, \xor ;

  assign \and  = SrcA & SrcB;  // AND_Gate and_1, 32 bits wide
  assign \or  = SrcA | SrcB;  // OR_Gate or_1, 32 bits wide
  Adder #(.width(32)) adder_1 (.a(SrcA), .b(SrcB), .out(add));  // open: cin, cout
  Subtractor #(.width(32)) subtractor_1 (.a(SrcA), .b(SrcB), .out(AsubB));  // open: bin, bout
  Subtractor #(.width(32)) subtractor_2 (.a(SrcB), .b(SrcA), .out(BsubA));  // open: bin, bout
  assign \xor  = SrcA ^ SrcB;  // XOR_Gate xor_1, 32 bits wide
  Shifter #(.width(32)) shifter_1 (.in(SrcB), .\dist (Shamt), .out(sll));
  Shifter #(.width(32)) shifter_2 (.in(SrcB), .\dist (SrcA[4:0]), .out(sllv));
  Comparator #(.width(32)) comparator_1 (.a(SrcA), .b(SrcB), .gt(gt), .eq(eq), .lt(lt));
  Comparator #(.width(32), .mode("unsigned")) comparator_2 (.a(SrcA), .b(SrcB), .gt(gtu), .lt(ltu));  // open: eq
  assign bit_extender_1_out = {{31{1'b0}}, lt};  // Bit_Extender bit_extender_1
  Multiplexer #(.select(4), .width(32), .disabled(0), .enable("false")) multiplexer_1 (
    .in0(\and ), .in1(\or ), .in2(add), .in3(AsubB), .in4(BsubA), .in5(\xor ),
    .in6({SrcB[15:0], {16{1'b0}}}), .in7(sll), .in8(sllv), .in9(bit_extender_1_out), .out(Out), .sel(Ctrl));  // open: in10, in11, in12, in13, in14, in15
  Multiplexer #(.select(4), .disabled(0), .enable("false")) multiplexer_2 (
    .in0(ltu), .in1(gtu), .in2(eq), .in3(lt), .in4(gt), .in5(1'b0), .in6(1'b0), .in7(1'b0), .in8(1'b0),
    .in9(1'b0), .in10(1'b0), .in11(1'b0), .in12(1'b0), .in13(1'b0), .in14(1'b0), .in15(1'b0), .out(Flag),
    .sel(Ctrl));

  // Other names for the same wires on the sheet: A[31:0] = SrcA; B[31:0] = SrcB; sll16[31:16] = SrcB[15:0]
endmodule

module NPC (
  input  [31:0] PC,
  input  [15:0] Offset,
  input  BrFlag,
  input  [2:0] Ctrl,
  input  [25:0] Index,
  input  [31:0] Reg,
  output [31:0] PCAdd4,
  output [31:0] NextPC
);

  wire [15:0] multiplexer_1_out;
  wire [31:0] adder_2_out, bit_extender_1_out;

  Multiplexer #(.width(16), .disabled(0), .enable("false")) multiplexer_1 (
    .in0({16{1'b0}}), .in1(Offset), .out(multiplexer_1_out), .sel(BrFlag));
  Adder #(.width(32)) adder_1 (.a(32'h4), .b(PC), .out(PCAdd4));  // open: cin, cout
  assign bit_extender_1_out = {{14{multiplexer_1_out[15]}}, {multiplexer_1_out, 2'b00}};  // Bit_Extender bit_extender_1
  Adder #(.width(32)) adder_2 (.a(PCAdd4), .b(bit_extender_1_out), .out(adder_2_out));  // open: cin, cout
  Multiplexer #(.select(3), .width(32), .disabled(0), .enable("false")) multiplexer_2 (
    .in0(PCAdd4), .in1(adder_2_out), .in2({PC[31:28], Index, 2'b00}), .in3(Reg), .out(NextPC), .sel(Ctrl));  // open: in4, in5, in6, in7
endmodule

module Controller (
  input  [5:0] Op,
  input  [5:0] Funct,
  output RegWrite,
  output EXTCtrl,
  output ALUSrc,
  output MemWrite,
  output [2:0] NPCCtrl,
  output [1:0] RegDst,
  output [1:0] DataToReg,
  output [3:0] ALUCtrl,
  output [1:0] DMCtrl
);

  wire addi, addu, \and , beq, j, jal, jr, lb, lh, lui, lw, not_1_out, not_2_out, not_3_out, not_4_out,
       not_5_out, not_6_out, not_7_out, not_8_out, not_9_out, not_10_out, not_11_out, not_12_out, \or , ori,
       R, sb, sh, sll, sllv, slt, subu, sw;

  not not_1 (not_1_out, Op[4]);
  not not_2 (not_2_out, Op[5]);
  buf or_1 (RegDst[1], jal);  // OR_Gate
  not not_3 (not_3_out, Op[3]);
  not not_4 (not_4_out, Op[2]);
  not not_5 (not_5_out, Op[1]);
  buf or_2 (RegDst[0], R);  // OR_Gate
  not not_6 (not_6_out, Op[0]);
  or or_3 (RegWrite, R, lh, ori, lw, lui, addi, jal, lb);
  and and_1 (R, not_2_out, not_1_out, not_3_out, not_4_out, not_5_out, not_6_out);
  and and_2 (ori, not_2_out, not_1_out, Op[3], Op[2], not_5_out, Op[0]);
  and and_3 (lw, Op[5], not_1_out, not_3_out, not_4_out, Op[1], Op[0]);
  and and_4 (beq, not_2_out, not_1_out, not_3_out, Op[2], not_5_out, not_6_out);
  and and_5 (lui, not_2_out, not_1_out, Op[3], Op[2], Op[1], Op[0]);
  and and_6 (j, not_2_out, not_1_out, not_3_out, not_4_out, Op[1], not_6_out);
  and and_7 (sw, Op[5], not_1_out, Op[3], not_4_out, Op[1], Op[0]);
  and and_8 (addi, not_2_out, not_1_out, Op[3], not_4_out, not_5_out, not_6_out);
  and and_9 (jal, not_2_out, not_1_out, not_3_out, not_4_out, Op[1], Op[0]);
  and and_10 (sh, Op[5], not_1_out, Op[3], not_4_out, not_5_out, Op[0]);
  and and_11 (sb, Op[5], not_1_out, Op[3], not_4_out, not_5_out, not_6_out);
  and and_12 (lh, Op[5], not_1_out, not_3_out, not_4_out, not_5_out, Op[0]);
  and and_13 (lb, Op[5], not_1_out, not_3_out, not_4_out, not_5_out, not_6_out);
  or or_4 (EXTCtrl, addi, sh, sb, lh, lb, lw, sw);
  not not_7 (not_7_out, Funct[5]);
  not not_8 (not_8_out, Funct[4]);
  or or_5 (ALUSrc, sh, ori, lw, sw, lui, addi, sb, lh, lb);
  not not_9 (not_9_out, Funct[3]);
  not not_10 (not_10_out, Funct[1]);
  not not_11 (not_11_out, Funct[2]);
  or or_6 (MemWrite, sw, sh, sb);
  not not_12 (not_12_out, Funct[0]);
  buf or_7 (DataToReg[1], jal);  // OR_Gate
  and and_14 (addu, R, Funct[5], not_8_out, not_9_out, not_11_out, not_10_out, Funct[0]);
  and and_15 (subu, R, Funct[5], not_8_out, not_9_out, not_11_out, Funct[1], Funct[0]);
  and and_16 (sll, R, not_7_out, not_8_out, not_9_out, not_11_out, not_10_out, not_12_out);
  and and_17 (\and , R, Funct[5], not_8_out, not_9_out, Funct[2], not_10_out, not_12_out);
  and and_18 (\or , R, Funct[5], not_8_out, not_9_out, Funct[2], not_10_out, Funct[0]);
  and and_19 (sllv, R, not_7_out, not_8_out, not_9_out, Funct[2], not_10_out, not_12_out);
  and and_20 (slt, R, Funct[5], not_8_out, Funct[3], not_11_out, Funct[1], not_12_out);
  and and_21 (jr, R, not_7_out, not_8_out, Funct[3], not_11_out, not_10_out, not_12_out);
  or or_8 (DataToReg[0], lw, lh, lb);
  buf or_9 (NPCCtrl[2], 1'b0);  // OR_Gate
  or or_10 (NPCCtrl[1], j, jr, jal);
  or or_11 (NPCCtrl[0], beq, jr);
  or or_12 (ALUCtrl[3], sllv, slt);
  or or_13 (ALUCtrl[2], lui, sll);
  or or_14 (ALUCtrl[1], sh, sb, lh, addu, subu, lw, sw, beq, lui, sll, addi, lb);
  or or_15 (ALUCtrl[0], subu, ori, sll, \or , slt);
  or or_16 (DMCtrl[1], sb, lb);
  or or_17 (DMCtrl[0], sh, lh);

  // Other names for the same wires on the sheet: f0 = Funct[0]; f1 = Funct[1]; f2 = Funct[2]; f3 = Funct[3];
  //   f4 = Funct[4]; f5 = Funct[5]
endmodule
