// Logisim project 2的n次方mod5_2进制编码.circ as structural Verilog: 2 circuits, main circuit mod5
module mod5 (
  input  In,
  output S0,
  output S1,
  output S2,
  output S3,
  output S4
);

  wire clock_1_out, register_1_q, register_2_q, state_trans_1_s0_2, state_trans_1_s1_2;
  wire [1:0] state_trans_2_s0_2;

  state_trans state_trans_1 (
    .S0(register_1_q), .S1(register_2_q), .In(In), .S0_2(state_trans_1_s0_2), .S1_2(state_trans_1_s1_2));
  Clock clock_1 (.out(clock_1_out));
  Register #(.width(1)) register_1 (
    .D(state_trans_1_s0_2), .en(1'b1), .Q(register_1_q), .clk(clock_1_out));  // open: clr
  Register #(.width(1)) register_2 (
    .D(state_trans_1_s1_2), .en(1'b1), .Q(register_2_q), .clk(clock_1_out));  // open: clr
  state_trans state_trans_2 (
    .S0(register_1_q), .S1(register_2_q), .In(In), .S0_2(state_trans_2_s0_2[0]), .S1_2(state_trans_2_s0_2[1]));
  Decoder #(.select(2), .enable("false")) decoder_1 (
    .out0(S1), .out1(S2), .out2(S3), .out3(S4), .sel(state_trans_2_s0_2));

  assign S0 = 1'b0;
endmodule

module state_trans (
  input  S0,
  input  S1,
  input  In,
  output S0_2,
  output S1_2
);

  wire and_1_out, and_2_out, and_3_out, and_4_out, and_5_out, and_6_out, and_7_out, and_8_out, and_9_out,
       and_10_out, not_1_out, not_2_out, not_3_out, not_4_out, not_5_out, not_6_out, not_7_out, not_8_out,
       or_2_out, or_3_out;

  not not_1 (not_1_out, S0);
  not not_2 (not_2_out, S1);
  not not_3 (not_3_out, S0);
  not not_4 (not_4_out, S1);
  not not_5 (not_5_out, S0);
  not not_6 (not_6_out, S1);
  and and_1 (and_1_out, not_1_out, not_2_out);
  and and_2 (and_2_out, not_3_out, S1);
  not not_7 (not_7_out, In);
  and and_3 (and_3_out, S0, not_4_out);
  not not_8 (not_8_out, In);
  and and_4 (and_4_out, S0, S1);
  and and_5 (and_5_out, not_5_out, S1);
  and and_6 (and_6_out, S0, not_6_out);
  and and_7 (and_7_out, and_1_out, In);
  and and_8 (and_8_out, and_2_out, not_7_out);
  and and_9 (and_9_out, and_3_out, not_8_out);
  and and_10 (and_10_out, and_4_out, In);
  or or_1 (S1_2, and_5_out, and_6_out);
  or or_2 (or_2_out, and_7_out, and_8_out);
  or or_3 (or_3_out, and_9_out, and_10_out);
  or or_4 (S0_2, or_2_out, or_3_out);
endmodule
