// Logisim project 2的n次方mod5_独热编码.circ as structural Verilog: 4 circuits, main circuit mod5
module mod5 (
  input  In,
  output S0,
  output S1,
  output S2,
  output S3,
  output S4
);

  wire [3:0] state_store_1_s, state_trans_1_s_prime;

  state_trans state_trans_1 (.In(In), .S(state_store_1_s), .S_prime(state_trans_1_s_prime));
  state_store state_store_1 (.S_prime(state_trans_1_s_prime), .S(state_store_1_s));
  \output  output_1 (.In(In), .S(state_store_1_s), .S0(S0), .S1(S1), .S2(S2), .S3(S3), .S4(S4));
endmodule

// S'
module state_trans (
  input  In,
  input  [3:0] S,
  output [3:0] S_prime
);

  wire and_1_out, and_2_out, and_3_out, and_4_out, and_5_out, and_6_out, and_7_out, and_8_out, not_1_out,
       not_2_out, not_3_out, not_4_out;

  and and_1 (and_1_out, S[0], not_1_out);
  not not_1 (not_1_out, In);
  and and_2 (and_2_out, S[3], not_2_out);
  not not_2 (not_2_out, In);
  and and_3 (and_3_out, S[0], In);
  and and_4 (and_4_out, S[3], In);
  and and_5 (and_5_out, S[1], In);
  and and_6 (and_6_out, S[2], In);
  and and_7 (and_7_out, S[1], not_3_out);
  not not_3 (not_3_out, In);
  and and_8 (and_8_out, S[2], not_4_out);
  not not_4 (not_4_out, In);
  or or_1 (S_prime[0], and_1_out, and_2_out);
  or or_2 (S_prime[1], and_3_out, and_4_out);
  or or_3 (S_prime[2], and_5_out, and_6_out);
  or or_4 (S_prime[3], and_7_out, and_8_out);
endmodule

module state_store (
  input  [3:0] S_prime,
  output [3:0] S
);

  wire clock_1_out, counter_1_q;
  wire [3:0] register_1_q;

  Clock clock_1 (.out(clock_1_out));
  Register #(.width(4)) register_1 (.D(S_prime), .en(1'b1), .Q(register_1_q), .clk(clock_1_out));  // open: clr
  Counter #(.width(1), .max('h1), .ongoal("stay")) counter_1 (
    .Q(counter_1_q), .clk(clock_1_out));  // open: load, D, count, carry, clr
  Multiplexer #(.width(4), .enable("false")) multiplexer_1 (
    .in0(4'b0001), .in1(register_1_q), .out(S), .sel(counter_1_q));
endmodule

module \output  (
  input  In,
  input  [3:0] S,
  output S0,
  output S1,
  output S2,
  output S3,
  output S4
);

  state_trans state_trans_1 (.In(In), .S(S), .S_prime({S4, S3, S2, S1}));

  assign S0 = 1'b0;
endmodule
