// Logisim project fibonacci.circ as structural Verilog: 1 circuit, main circuit main
module main (
  input  [2:0] In,
  output [3:0] Nth
);

  wire clock_1_out, comparator_1_eq, counter_1_q;
  wire [2:0] counter_2_q;
  wire [3:0] adder_1_out, multiplexer_1_out, register_1_q, register_2_q;

  Clock clock_1 (.out(clock_1_out));
  Counter #(.width(1), .max('h1), .ongoal("stay")) counter_1 (
    .Q(counter_1_q), .clk(clock_1_out));  // open: load, D, count, carry, clr
  Multiplexer #(.width(4), .enable("false")) multiplexer_1 (
    .in0(4'b0001), .in1(adder_1_out), .out(multiplexer_1_out), .sel(counter_1_q));
  Register #(.width(4)) register_1 (.D(multiplexer_1_out), .Q(register_1_q), .clk(clock_1_out));  // open: en, clr
  Register #(.width(4)) register_2 (.D(register_1_q), .Q(register_2_q), .clk(clock_1_out));  // open: en, clr
  Counter #(.width(3), .max('h7), .ongoal("stay")) counter_2 (
    .Q(counter_2_q), .clk(clock_1_out));  // open: load, D, count, carry, clr
  Adder #(.width(4)) adder_1 (.a(register_1_q), .b(register_2_q), .out(adder_1_out));  // open: cin, cout
  Register #(.width(4)) register_3 (.D(register_1_q), .Q(Nth), .clk(comparator_1_eq));  // open: en, clr
  Comparator #(.width(3)) comparator_1 (.a(In), .b(counter_2_q), .eq(comparator_1_eq));  // open: gt, lt
endmodule
