// Logisim project fibonacci_quickpower.circ as structural Verilog: 5 circuits, main circuit main
module main (
  input  [31:0] N,
  output [31:0] Nth
);

  wire comparator_1_eq;
  wire [31:0] multiplexer_1_out, subtractor_1_out;

  Comparator #(.width(32)) comparator_1 (.a({32{1'b0}}), .b(N), .eq(comparator_1_eq));  // open: gt, lt
  Subtractor #(.width(32)) subtractor_1 (.a(N), .b(32'h1), .out(subtractor_1_out));  // open: bin, bout
  Multiplexer #(.width(32), .enable("false")) multiplexer_1 (
    .in0(subtractor_1_out), .in1({32{1'b0}}), .out(multiplexer_1_out), .sel(comparator_1_eq));
  quick_power quick_power_1 (
    .B1(Nth), .N(multiplexer_1_out), .A1(32'h1), .A2(32'h1), .A3(32'h1), .A4({32{1'b0}}));  // open: B2, B3, B4
endmodule

module quick_power (
  input  [31:0] A1,
  input  [31:0] A2,
  input  [31:0] A3,
  input  [31:0] A4,
  input  [31:0] N,
  output [31:0] B1,
  output [31:0] B2,
  output [31:0] B3,
  output [31:0] B4
);

  wire clk, comparator_1_eq, counter_1_q, is_odd;
  wire [31:0] a1_t, a2_t, a3_t, a4_t, b1_t, b2_t, b3_t, b4_t, mul_1_c00, mul_1_c01, mul_1_c10, mul_1_c11,
       mul_2_c00, mul_2_c01, mul_2_c10, mul_2_c11, multiplexer_2_out, multiplexer_3_out, multiplexer_4_out,
       multiplexer_5_out, register_1_q;
  wire [31:1] multiplexer_1_out;

  Clock clock_1 (.out(clk));
  matrix matrix_1 (
    .D00(A1), .A00(mul_1_c00), .D01(A2), .A01(mul_1_c01), .D10(A3), .A10(mul_1_c10), .D11(A4),
    .A11(mul_1_c11), .clk(clk), .A00_2(a1_t), .A01_2(a2_t), .A10_2(a3_t), .A11_2(a4_t));
  Multiplexer #(.width(32), .enable("false")) multiplexer_1 (
    .in0(N), .in1(register_1_q), .out({multiplexer_1_out, is_odd}), .sel(counter_1_q));
  Counter #(.width(1), .max('h1), .ongoal("stay")) counter_1 (
    .Q(counter_1_q), .clk(clk));  // open: load, D, count, carry, clr
  Comparator #(.width(32)) comparator_1 (
    .a({multiplexer_1_out, is_odd}), .b({32{1'b0}}), .eq(comparator_1_eq));  // open: gt, lt
  mul mul_1 (
    .A00(a1_t), .A01(a2_t), .A10(a3_t), .A11(a4_t), .B00(a1_t), .B01(a2_t), .B10(a3_t), .B11(a4_t),
    .C00(mul_1_c00), .C01(mul_1_c01), .C10(mul_1_c10), .C11(mul_1_c11));
  Register #(.width(32)) register_1 (.D({1'b0, multiplexer_1_out}), .Q(register_1_q), .clk(clk));  // open: en, clr
  Register #(.width(32)) register_2 (.D(b1_t), .Q(B1), .clk(comparator_1_eq));  // open: en, clr
  Register #(.width(32)) register_3 (.D(b2_t), .Q(B2), .clk(comparator_1_eq));  // open: en, clr
  Register #(.width(32)) register_4 (.D(b3_t), .Q(B3), .clk(comparator_1_eq));  // open: en, clr
  Register #(.width(32)) register_5 (.D(b4_t), .Q(B4), .clk(comparator_1_eq));  // open: en, clr
  matrix matrix_2 (
    .D00(32'h1), .A00(multiplexer_2_out), .D01({32{1'b0}}), .A01(multiplexer_3_out), .D10({32{1'b0}}),
    .A10(multiplexer_4_out), .D11(32'h1), .A11(multiplexer_5_out), .clk(clk), .A00_2(b1_t), .A01_2(b2_t),
    .A10_2(b3_t), .A11_2(b4_t));
  mul mul_2 (
    .A00(a1_t), .A01(a2_t), .A10(a3_t), .A11(a4_t), .B00(b1_t), .B01(b2_t), .B10(b3_t), .B11(b4_t),
    .C00(mul_2_c00), .C01(mul_2_c01), .C10(mul_2_c10), .C11(mul_2_c11));
  Multiplexer #(.width(32), .enable("false")) multiplexer_2 (
    .in0(b1_t), .in1(mul_2_c00), .out(multiplexer_2_out), .sel(is_odd));
  Multiplexer #(.width(32), .enable("false")) multiplexer_3 (
    .in0(b2_t), .in1(mul_2_c01), .out(multiplexer_3_out), .sel(is_odd));
  Multiplexer #(.width(32), .enable("false")) multiplexer_4 (
    .in0(b3_t), .in1(mul_2_c10), .out(multiplexer_4_out), .sel(is_odd));
  Multiplexer #(.width(32), .enable("false")) multiplexer_5 (
    .in0(b4_t), .in1(mul_2_c11), .out(multiplexer_5_out), .sel(is_odd));
endmodule

module mul (
  input  [31:0] A00,
  input  [31:0] A01,
  input  [31:0] A10,
  input  [31:0] A11,
  input  [31:0] B00,
  input  [31:0] B01,
  input  [31:0] B10,
  input  [31:0] B11,
  output [31:0] C00,
  output [31:0] C01,
  output [31:0] C10,
  output [31:0] C11
);

  wire [31:0] multiplier_1_out, multiplier_2_out, multiplier_3_out, multiplier_4_out, multiplier_5_out,
       multiplier_6_out, multiplier_7_out, multiplier_8_out;

  Multiplier #(.width(32)) multiplier_1 (.a(A00), .b(B00), .out(multiplier_1_out));  // open: cin, cout
  Adder #(.width(32)) adder_1 (.a(multiplier_1_out), .b(multiplier_2_out), .out(C00));  // open: cin, cout
  Multiplier #(.width(32)) multiplier_2 (.a(A01), .b(B10), .out(multiplier_2_out));  // open: cin, cout
  Multiplier #(.width(32)) multiplier_3 (.a(A00), .b(B01), .out(multiplier_3_out));  // open: cin, cout
  Adder #(.width(32)) adder_2 (.a(multiplier_3_out), .b(multiplier_4_out), .out(C01));  // open: cin, cout
  Multiplier #(.width(32)) multiplier_4 (.a(A01), .b(B11), .out(multiplier_4_out));  // open: cin, cout
  Multiplier #(.width(32)) multiplier_5 (.a(A10), .b(B00), .out(multiplier_5_out));  // open: cin, cout
  Adder #(.width(32)) adder_3 (.a(multiplier_5_out), .b(multiplier_6_out), .out(C10));  // open: cin, cout
  Multiplier #(.width(32)) multiplier_6 (.a(A11), .b(B10), .out(multiplier_6_out));  // open: cin, cout
  Multiplier #(.width(32)) multiplier_7 (.a(A10), .b(B01), .out(multiplier_7_out));  // open: cin, cout
  Adder #(.width(32)) adder_4 (.a(multiplier_7_out), .b(multiplier_8_out), .out(C11));  // open: cin, cout
  Multiplier #(.width(32)) multiplier_8 (.a(A11), .b(B11), .out(multiplier_8_out));  // open: cin, cout
endmodule

module matrix (
  input  [31:0] D00,
  input  [31:0] A00,
  input  [31:0] D01,
  input  [31:0] A01,
  input  [31:0] D10,
  input  [31:0] A10,
  input  [31:0] D11,
  input  [31:0] A11,
  input  clk,
  output [31:0] A00_2,
  output [31:0] A01_2,
  output [31:0] A10_2,
  output [31:0] A11_2
);

  wire counter_1_q;
  wire [31:0] register_1_q, register_2_q, register_3_q, register_4_q;

  Register #(.width(32)) register_1 (.D(A00), .Q(register_1_q), .clk(clk));  // open: en, clr
  Register #(.width(32)) register_2 (.D(A01), .Q(register_2_q), .clk(clk));  // open: en, clr
  Register #(.width(32)) register_3 (.D(A10), .Q(register_3_q), .clk(clk));  // open: en, clr
  Register #(.width(32)) register_4 (.D(A11), .Q(register_4_q), .clk(clk));  // open: en, clr
  Multiplexer #(.width(32), .enable("false")) multiplexer_1 (
    .in0(D00), .in1(register_1_q), .out(A00_2), .sel(counter_1_q));
  Multiplexer #(.width(32), .enable("false")) multiplexer_2 (
    .in0(D01), .in1(register_2_q), .out(A01_2), .sel(counter_1_q));
  Multiplexer #(.width(32), .enable("false")) multiplexer_3 (
    .in0(D10), .in1(register_3_q), .out(A10_2), .sel(counter_1_q));
  Multiplexer #(.width(32), .enable("false")) multiplexer_4 (
    .in0(D11), .in1(register_4_q), .out(A11_2), .sel(counter_1_q));
  Counter #(.width(1), .max('h1), .ongoal("stay")) counter_1 (
    .Q(counter_1_q), .clk(clk));  // open: load, D, count, carry, clr
endmodule

module test (
  input  [1:0] in_1,
  output [31:0] out_2,
  output halt
);

  wire clock_1_out;
  wire [31:0] rom_1_data;

  Counter #(.max('h40), .ongoal("stay")) counter_1 (.carry(halt), .clk(clock_1_out));  // open: load, D, count, Q, clr
  Clock clock_1 (.out(clock_1_out));
  ROM #(.addrWidth(2), .dataWidth(32)) rom_1 (.addr(in_1), .data(rom_1_data));  // open: sel
  main main_1 (.N(rom_1_data), .Nth(out_2));

  // Notes on the sheet:
  //   contents of rom_1 (hex, n*v repeats v):
  //   1 11111111 1 1
endmodule
