// Logisim project my_mult.circ as structural Verilog: 2 circuits, main circuit main
module main (
  input  [3:0] in_1,
  input  [3:0] in_2,
  output out_3
);

  wire [3:0] multiplier_1_cout, multiplier_1_out, n4bit_unsigned_mult_1_hi, n4bit_unsigned_mult_1_lo;

  _4bit_unsigned_mult u_4bit_unsigned_mult_1 (
    .A(in_1), .B(in_2), .HI(n4bit_unsigned_mult_1_hi), .LO(n4bit_unsigned_mult_1_lo));
  Multiplier #(.width(4)) multiplier_1 (
    .a(in_1), .b(in_2), .out(multiplier_1_out), .cout(multiplier_1_cout));  // open: cin
  // Probe on {n4bit_unsigned_mult_1_hi, n4bit_unsigned_mult_1_lo}
  // Probe on {multiplier_1_cout, multiplier_1_out}
  Comparator comparator_1 (
    .a({n4bit_unsigned_mult_1_hi, n4bit_unsigned_mult_1_lo}), .b({multiplier_1_cout, multiplier_1_out}),
    .eq(out_3));  // open: gt, lt
endmodule

module _4bit_unsigned_mult (
  input  [3:0] A,
  input  [3:0] B,
  output [3:0] HI,
  output [3:0] LO
);

  wire clk, comparator_1_eq, counter_1_q;
  wire [2:0] counter_2_q;
  wire [3:0] adder_1_out, high, low, multiplexer_1_out, multiplexer_2_out;
  wire [4:4] adder_1_cout;

  Clock clock_1 (.out(clk));
  Multiplexer #(.width(4), .enable("false")) multiplexer_1 (
    .in0(4'b0000), .in1(A), .out(multiplexer_1_out), .sel(multiplexer_2_out[0]));
  Counter #(.width(1), .max('h1), .ongoal("stay")) counter_1 (
    .Q(counter_1_q), .clk(clk));  // open: load, D, count, carry, clr
  Adder #(.width(4)) adder_1 (.a(multiplexer_1_out), .b(high), .out(adder_1_out), .cout(adder_1_cout[4]));  // open: cin
  Multiplexer #(.width(4), .enable("false")) multiplexer_2 (
    .in0(B), .in1(low), .out(multiplexer_2_out), .sel(counter_1_q));
  Register #(.width(4)) register_1 (.D({adder_1_cout[4], adder_1_out[3:1]}), .Q(high), .clk(clk));  // open: en, clr
  Register #(.width(4)) register_2 (.D({adder_1_out[0], multiplexer_2_out[3:1]}), .Q(low), .clk(clk));  // open: en, clr
  Counter #(.width(3), .max('h4), .ongoal("stay")) counter_2 (
    .Q(counter_2_q), .clk(clk));  // open: load, D, count, carry, clr
  Comparator #(.width(3), .mode("unsigned")) comparator_1 (
    .a(counter_2_q), .b(3'b100), .eq(comparator_1_eq));  // open: gt, lt
  Register #(.width(4)) register_3 (.D(high), .Q(HI), .clk(comparator_1_eq));  // open: en, clr
  Register #(.width(4)) register_4 (.D(low), .Q(LO), .clk(comparator_1_eq));  // open: en, clr
endmodule
