// Logisim project test.circ as structural Verilog: 4 circuits, main circuit main
module main (
  input  [7:0] in_1,
  input  in_2,
  output [7:0] out_3
);

  wire clock_1_out;

  Clock clock_1 (.out(clock_1_out));
  Register register_1 (.D(in_1), .Q(out_3), .clk(clock_1_out), .clr(in_2));  // open: en
endmodule

module sr_latch (
  input  R,
  input  S,
  output Q,
  output nQ
);

  wire or_1_out, or_2_out;

  or or_1 (or_1_out, R, nQ);
  or or_2 (or_2_out, Q, S);
  not not_1 (Q, or_1_out);
  not not_2 (nQ, or_2_out);
endmodule

module d_latch (
  input  CLK,
  input  D,
  output Q,
  output nQ
);

  wire and_1_out, and_2_out, not_1_out;

  and and_1 (and_1_out, CLK, not_1_out);
  not not_1 (not_1_out, D);
  and and_2 (and_2_out, CLK, D);
  sr_latch sr_latch_1 (.R(and_1_out), .S(and_2_out), .Q(Q), .nQ(nQ));
endmodule

module d_flip_flop (
  input  in_1,
  input  D,
  output Q
);

  wire d_latch_1_p3, not_1_out;

  not not_1 (not_1_out, in_1);
  // d_latch d_latch_1: pin names not known; wires that end beside it: D, not_1_out, d_latch_1_p3
  // d_latch d_latch_2: pin names not known; wires that end beside it: d_latch_1_p3, in_1, Q
endmodule
